# Fritzing sketch wireing (saved by Fritzing 0.9.3b)
breadboards: 1

parts:
  Taster_/_Buzzer = Pushbutton [package="[SMD]"]
  Arduino = Pro Micro

nets:
  N1: Taster_/_Buzzer.Pin_1, Taster_/_Buzzer.Pin_2, Arduino.GND
  N2: Taster_/_Buzzer.Pin_3, Taster_/_Buzzer.Pin_4, Arduino.D9

custom parts:
  Pro Micro: The SparkFun Pro Micro is a complete USB-based microcontoller development system, in a very small footprint, capable of implementing many types of projects. All programming can be done via the USB port.
